# Fritzing sketch Aigis node (saved by Fritzing 0.9.4)
breadboards: 1

parts:
  VCC1 = Battery  # not connected
  Power_plug1 = Power plug
  S1 = Toggle Switch [package=THT]
  Part1 = Arduino Nano (Rev3.0)
  J2 = Piezo Speaker
  J3 = Basic Servo
  J5 = Basic Servo
  J6 = Basic Servo
  J7 = Basic Servo

nets:
  GND: Power_plug1.GND, Part1.GND, J2.pin1, J3.gnd, J5.gnd, J6.gnd, J7.gnd
  VCC: Power_plug1.VCC, S1.L2, Part1.VIN, J3.vcc, J5.vcc, J6.vcc, J7.vcc
  N1: Part1.D2, J7.pulse
  N2: Part1.D3, J5.pulse
  N3: Part1.D4, J6.pulse
  N4: Part1.D5, J3.pulse
  N5: Part1.D13/SCK, J2.pin2

notes:
  LEFT LEG
  RIGHT LEG
  LEFT FOOT
  RIGHT FOOT
  Pink Wire will take UART data from GPIO 42 of ESPBOX3 to RX of Arduino nano

custom parts:
  Battery: Your standard 2x 18650 battery pack (7.4 Volts)
