# Fritzing sketch Dore Node CKT DIA  (saved by Fritzing 0.9.4)
breadboards: 1

parts:
  Mod1 = ESP32 - CAM
  Part1 = HC-SR501 Body Sensor Module
  M1 = 1 chan 5v relay module
  JACK1 = 2.1mm Barrel Jack with Terminal Block
  U1 = Micro USB B Connectors DIP [package=usb-ab-micro-smd]

nets:
  5V: Mod1.5V, Part1.VCC, M1.pin_1, U1.VBUS
  GND: Mod1.GND, Part1.GND, M1.pin_2, U1.GND
  N1: Mod1.IO13, Part1.OUT
  N2: Mod1.IO16, M1.pin_3
  N3: M1.pin_4, JACK1.NEG

notes:
  5v / 2A Adapter microUSB supply
  12v / 1A Power adapter
  Aigis Dore Node
  Circuit Diagram

custom parts:
  ESP32 - CAM: The ESP32-CAM has a very competitive small-size camera module that can operate independently as a minimum system with a footprint of only 27*40.5*4.5mm and a deep sleep current of up to 6mA.
  HC-SR501 Body Sensor Module: Pyroelectric Infrared PIR Motion Sensor Detector Module
  1 chan 5v relay module: 1 Channel 5V Relay Module Board Shield with Optocoupler Support High and Low Level Trigger for Arduino.
  Micro USB B Connectors DIP: USB Connectors AE-USB-MICRO-B-D K-06656
