# Fritzing sketch Health Node (saved by Fritzing 0.9.4)
breadboards: 1

parts:
  U1 = LIPO-110mAh [package=lipo-110]
  A1 = XIAO ESP32C3-tht
  Part1 = InvenSense MPU6050
  M1 = MakerFocus MAX30102
  S3 = Toggle Switch [package=THT]
  J1 = Piezo Speaker

nets:
  N1: U1.+, A1.Pin_8
  N2: U1.-, S3.COM
  N3: A1.Pin_7, S3.L2
  N4: A1.Pin_15, Part1.SCL, M1.SCL
  N5: A1.Pin_16, Part1.SDA, M1.SDA
  N6: A1.Pin_17, J1.pin2
  VCC: A1.Pin_20, Part1.VCC, M1.VIN
  GND: A1.Pin_21, Part1.GND, M1.GND, J1.pin1

custom parts:
  XIAO ESP32C3-tht: Seeed Studio XIAO ESP32C3 adopts new RISC-V architecture, supporting both Wi-Fi and BLE wireless connectivities.
  MakerFocus MAX30102: Oximeter module using the MAX30102 chip. As usual, if you want the mounting holes in pcb, you need to drag a hole over the pad in silkscreen to actually drill the hole (by default they are not drilled)
