# Fritzing sketch Smart Home Node CKD Dia (saved by Fritzing 0.9.4)
breadboards: 1

parts:
  M1 = ac light dimmer-4terminal
  U1 = ESP32-38PinWide [part_number=ESP32-38PinWide]
  U2 = 2-Channel 5v Relay Shield [package=relay-2ch5v10a]
  Mod1 = generic-ac-power-supply [package=THT]
  J1 = Screw terminal - 2 pins [package=THT]

nets:
  VCC: M1.VCC, U1.VIN, U2.VCC, Mod1.pin3#2
  GND: M1.GND, U1.GPIO11, U2.GND, Mod1.pin3#3
  N1: M1.Z-C, U1.GPIO27
  N2: M1.PWM, U1.GPIO26
  N3: M1.AC-IN1, U2.K1-On, U2.K2-On, Mod1.pin2, J1.pin1
  N4: M1.AC-IN2, Mod1.pin1, J1.pin2
  N5: U1.GPIO22, U2.IN2
  N6: U1.GPIO23, U2.IN1

notes:
  Alternating current power supply
  5v / 1A DC Power supply
  Touch 1
  Touch 4
  Touch 3
  Touch 2

custom parts:
  ac light dimmer-4terminal: ac light dimmer module 4terminal.
  ESP32-38PinWide: Generic 38-Pin ESP32 with wide format (only access to one side of pins on a breadboard) based on Stephen Lilley's HiLetgo ESP-WROOM-32 ESP32 ESP-32S Development Board.
  2-Channel 5v Relay Shield: 2 Channel 5v Relay Shield w. 2x SPD-06VDC-SD-C
  generic-ac-power-supply: Generic ac power supply module. Use as is, or customize the svgs to fit your particular device (as they are all different.) Provides AC input and single DC output. PCB is generic and will need modifications if you intend to do a pcb mount.
